// Logisim project ULA.circ as structural Verilog: 1 circuit, main circuit ULA
module ULA (
  input  [31:0] A,
  input  [31:0] B,
  input  [2:0] ALUControl,
  output sZero,
  output [31:0] Result
);

  wire comparator_1_lt, comparator_2_lt, extensorsinal_1_1_p1, extensorsinal_1_2_p1;
  wire [31:0] adder_1_out, and_1_out, extensorsinal_1_1_p3, extensorsinal_1_2_p3, multiplexer_1_out,
       multiplexer_2_out, or_1_out, shifter_1_out, shifter_2_out, shifter_3_out, subtractor_1_out, xor_1_out;

  // Probe on A
  // Probe on B
  Adder #(.width(32)) adder_1 (.a(A), .b(B), .out(adder_1_out));  // open: cin, cout
  Subtractor #(.width(32)) subtractor_1 (.a(A), .b(B), .out(subtractor_1_out));  // open: bin, bout
  Shifter #(.shift("lr"), .width(32)) shifter_1 (.in(A), .\dist (B[4:0]), .out(shifter_1_out));
  Shifter #(.shift("ar"), .width(32)) shifter_2 (.in(A), .\dist (B[4:0]), .out(shifter_2_out));
  Multiplexer #(.width(32)) multiplexer_1 (
    .in0(adder_1_out), .in1(subtractor_1_out), .out(multiplexer_1_out), .sel(extensorsinal_1_1_p1));
  Shifter #(.width(32)) shifter_3 (.in(A), .\dist (B[4:0]), .out(shifter_3_out));
  Comparator #(.width(32)) comparator_1 (.a(A), .b(B), .lt(comparator_1_lt));  // open: gt, eq
  Comparator #(.mode("unsigned"), .width(32)) comparator_2 (.a(A), .b(B), .lt(comparator_2_lt));  // open: gt, eq
  assign xor_1_out = A ^ B;  // XOR_Gate xor_1, 32 bits wide
  Multiplexer #(.width(32)) multiplexer_2 (
    .in0(shifter_1_out), .in1(shifter_2_out), .out(multiplexer_2_out), .sel(extensorsinal_1_2_p1));
  assign or_1_out = A | B;  // OR_Gate or_1, 32 bits wide
  assign and_1_out = A & B;  // AND_Gate and_1, 32 bits wide
  // extensorSinal_1 extensorsinal_1_1: pin names not known; wires that end beside it: extensorsinal_1_1_p1, comparator_1_lt, extensorsinal_1_1_p3
  // extensorSinal_1 extensorsinal_1_2: pin names not known; wires that end beside it: extensorsinal_1_2_p1, comparator_2_lt, extensorsinal_1_2_p3
  Multiplexer #(.select(3), .width(32)) multiplexer_3 (
    .in0(multiplexer_1_out), .in1(shifter_3_out), .in2(extensorsinal_1_1_p3), .in3(extensorsinal_1_2_p3),
    .in4(xor_1_out), .in5(multiplexer_2_out), .in6(or_1_out), .in7(and_1_out), .out(Result), .sel(ALUControl));
  // zero zero_1: pin names not known; wires that end beside it: sZero, Result

  // Other names for the same wires on the sheet: Shift[4:0] = B[4:0]
endmodule
