// Logisim project estagioID_EX.circ as structural Verilog: 1 circuit, main circuit estagioID_EX
module estagioID_EX (
  input  [31:0] PCplus4_ID,
  input  [6:0] opcode_ID,
  input  RegWrite_ID,
  input  Lui_ID,
  input  [31:0] PC_ID,
  input  [31:0] ld1_ID,
  input  ALUSrcB_ID,
  input  MemToReg_ID,
  input  [31:0] ld2_ID,
  input  PCSrc_ID,
  input  MemRead_ID,
  input  [4:0] rd_ID,
  input  Jump_ID,
  input  MemWrite_ID,
  input  [2:0] f3_ID,
  input  Jalr_ID,
  input  Branch_ID,
  input  [6:0] f7_ID,
  input  [1:0] ALUOp_ID,
  input  BranchSrc_ID,
  input  [31:0] imm_ID,
  input  Auipc_ID,
  input  CLK,
  output [31:0] PCplus4_EX,
  output [6:0] opcode_EX,
  output RegWrite_EX,
  output Lui_EX,
  output [31:0] PC_EX,
  output [31:0] ld1_EX,
  output ALUSrcB_EX,
  output MemToReg_EX,
  output [31:0] ld2_EX,
  output PCSrc_EX,
  output MemRead_EX,
  output [4:0] rd_EX,
  output Jump_EX,
  output MemWrite_EX,
  output [2:0] f3_EX,
  output Jalr_EX,
  output Branch_EX,
  output [6:0] f7_EX,
  output [1:0] ALUOp_EX,
  output BranchSrc_EX,
  output [31:0] imm_EX,
  output Auipc_EX
);

  Register #(.width(32)) PCplus4 (.D(PCplus4_ID), .en(1'b1), .clk(CLK), .Q(PCplus4_EX), .clr(1'b0));
  Register #(.width(32)) PC (.D(PC_ID), .en(1'b1), .clk(CLK), .Q(PC_EX), .clr(1'b0));
  Register #(.width(7)) opcode (.D(opcode_ID), .en(1'b1), .clk(CLK), .Q(opcode_EX), .clr(1'b0));
  Register #(.width(32)) ld1 (.D(ld1_ID), .en(1'b1), .clk(CLK), .Q(ld1_EX));  // open: clr
  Register #(.width(32)) ld2 (.D(ld2_ID), .en(1'b1), .clk(CLK), .Q(ld2_EX), .clr(1'b0));
  Register #(.width(5)) rd (.D(rd_ID), .en(1'b1), .clk(CLK), .Q(rd_EX), .clr(1'b0));
  Register #(.width(3)) funct3 (.D(f3_ID), .en(1'b1), .clk(CLK), .Q(f3_EX), .clr(1'b0));
  Register #(.width(7)) funct7 (.D(f7_ID), .en(1'b1), .clk(CLK), .Q(f7_EX), .clr(1'b0));
  Register #(.width(32)) imm (.D(imm_ID), .en(1'b1), .clk(CLK), .Q(imm_EX), .clr(1'b0));
  Register #(.width(1)) RegWrite (.D(RegWrite_ID), .en(1'b1), .clk(CLK), .Q(RegWrite_EX), .clr(1'b0));
  Register #(.width(1)) ALUSrc (.D(ALUSrcB_ID), .en(1'b1), .clk(CLK), .Q(ALUSrcB_EX));  // open: clr
  Register #(.width(1)) PCSrc (.D(PCSrc_ID), .en(1'b1), .clk(CLK), .Q(PCSrc_EX), .clr(1'b0));
  Register #(.width(1)) Jump (.D(Jump_ID), .en(1'b1), .clk(CLK), .Q(Jump_EX), .clr(1'b0));
  Register #(.width(1)) Jalr (.D(Jalr_ID), .en(1'b1), .clk(CLK), .Q(Jalr_EX), .clr(1'b0));
  Register #(.width(2)) ALUOp (.D(ALUOp_ID), .en(1'b1), .clk(CLK), .Q(ALUOp_EX), .clr(1'b0));
  Register #(.width(1)) Auipc (.D(Auipc_ID), .en(1'b1), .clk(CLK), .Q(Auipc_EX), .clr(1'b0));
  Register #(.width(1)) MemRead (.D(MemRead_ID), .en(1'b1), .clk(CLK), .Q(MemRead_EX), .clr(1'b0));
  Register #(.width(1)) Branch (.D(Branch_ID), .en(1'b1), .clk(CLK), .Q(Branch_EX), .clr(1'b0));
  Register #(.width(1)) BranchSrc (.D(BranchSrc_ID), .en(1'b1), .clk(CLK), .Q(BranchSrc_EX), .clr(1'b0));
  Register #(.width(1)) Lui (.D(Lui_ID), .en(1'b1), .clk(CLK), .Q(Lui_EX), .clr(1'b0));
  Register #(.width(1)) MemToReg (.D(MemToReg_ID), .en(1'b1), .clk(CLK), .Q(MemToReg_EX), .clr(1'b0));
  Register #(.width(1)) MemWrite (.D(MemWrite_ID), .en(1'b1), .clk(CLK), .Q(MemWrite_EX), .clr(1'b0));

  // Notes on the sheet:
  //   PC
  //   Decodificador
  //   ucPrincipal e ucDesvio
endmodule
