// Logisim project memdados.circ as structural Verilog: 1 circuit, main circuit datamem
// Mem. dados
module datamem (
  input  MemWrite,
  input  clk,
  input  [31:0] Escreve_dado,
  input  [31:0] Endereco,
  output [31:0] Dados_lidos
);

  wire not_1_out;

  RAM #(.addrWidth(24), .dataWidth(32), .trigger("falling")) ram_1 (
    .addr(Endereco[23:0]), .we(MemWrite), .oe(1'b1), .clk(not_1_out), .din(Escreve_dado), .dout(Dados_lidos));
  not not_1 (not_1_out, clk);
endmodule
