// Logisim project ucULA.circ as structural Verilog: 1 circuit, main circuit ucULA
module ucULA (
  input  [2:0] funct3,
  input  [1:0] ALUOp,
  output [2:0] ALUControl
);

  wire [2:0] multiplexer_1_out, multiplexer_2_out;

  Multiplexer #(.width(3)) multiplexer_1 (.in0(3'b010), .in1(3'b011), .out(multiplexer_1_out), .sel(funct3[1]));
  Multiplexer #(.width(3)) multiplexer_2 (
    .in0(3'b000), .in1(multiplexer_1_out), .out(multiplexer_2_out), .sel(funct3[2]));
  Multiplexer #(.select(2), .width(3)) multiplexer_3 (
    .in0(3'b000), .in1(multiplexer_2_out), .in2(funct3), .out(ALUControl), .sel(ALUOp));  // open: in3

  // Notes on the sheet:
  //   blt/bge
  //   bltu/bgeu
  //   funct3 >= 0x4
  //   beq/bne
  //   R-type/I-type
  //   lw/sw
  //   B-type
endmodule
