// Logisim project main.circ as structural Verilog: 1 circuit, main circuit main
module main (
);

  wire and_1_out, and_2_out, and_3_out, Branch_EX, BranchSrc, CLK, estagioex_mem_1_jump_mem,
       estagioex_mem_1_memread_mem, estagioex_mem_1_memtoreg_mem, estagioex_mem_1_memwrite_mem,
       estagioex_mem_1_regwrite_mem, estagioid_ex_1_p23, estagioid_ex_1_p25, estagioid_ex_1_p26,
       estagioid_ex_1_p27, estagioid_ex_1_p28, estagioid_ex_1_p30, estagioid_ex_1_p34, estagioid_ex_1_p35,
       estagioid_ex_1_p40, estagioid_ex_1_p41, estagioid_ex_1_p43, estagioid_ex_1_p44, estagioif_id_1_p5,
       estagioif_id_1_p7, estagiomem_wb_1_jump_wb, estagiomem_wb_1_memtoreg_wb, estagiomem_wb_1_regwrite_wb,
       Jalr_EX, Jump_WB, PCSrc_EX, RegWrite_WB, Stop, sUnsigned, ucprincipal_1_alusrcb,
       ucprincipal_1_auipc_uc, ucprincipal_1_branch, ucprincipal_1_jump, ucprincipal_1_lui_uc,
       ucprincipal_1_memread, ucprincipal_1_memtoreg, ucprincipal_1_memwrite, ucprincipal_1_pcsrc,
       ucprincipal_1_regwrite, ucprincipal_1_s_jalr, ula_1_szero, undriven;
  wire [1:0] offset, ucenderecamento_1_size, ucprincipal_1_aluop;
  wire [2:0] decodificador_1_funct3, estagioex_mem_1_f3_mem, estagioid_ex_1_p42;
  wire [3:0] ucenderecamento_1_byteenable, ucula_1_p5;
  wire [4:0] decodificador_1_rd, decodificador_1_rs1, decodificador_1_rs2, estagioex_mem_1_rd_mem,
       estagioid_ex_1_p45, estagiomem_wb_1_rd_wb, rd_WB;
  wire [6:0] decodificador_1_funct7, decodificador_1_opcode;
  wire [31:0] adder_1_out, adder_2_out, ALU, bancoregistradores_1_ld1, bancoregistradores_1_ld2,
       contadorciclos_1_contador, decodificador_1_imm, estagioex_mem_1_ld2_mem, estagioex_mem_1_pcplus4_mem,
       estagioid_ex_1_p33, estagioid_ex_1_p36, estagioid_ex_1_p37, estagioid_ex_1_p38, estagioid_ex_1_p39,
       estagioif_id_1_p8, estagioif_id_1_p9, estagiomem_wb_1_aluresult_wb, estagiomem_wb_1_memdata_wb,
       estagiomem_wb_1_pcplus4_wb, Imm, LD1, LD2, memdados_1_dados_lidos, meminstr_1_instruction,
       multiplexer_1_out, multiplexer_2_out, multiplexer_3_out, multiplexer_4_out, multiplexer_6_out, PC,
       PC_q, ula_1_result, WD;

  Multiplexer #(.width(32)) multiplexer_1 (
    .in0(adder_2_out), .in1(adder_1_out), .out(multiplexer_1_out), .sel(ucprincipal_1_pcsrc));
  Adder #(.width(32)) adder_1 (.a(PC_q), .b(decodificador_1_imm), .out(adder_1_out));  // open: cin, cout
  // Probe on Imm
  and and_1 (and_1_out, CLK, ~Stop);  // AND_Gate
  // Probe on contadorciclos_1_contador
  contadorCiclos contadorciclos_1 (.Clock(and_1_out), .Contador(contadorciclos_1_contador));
  Clock clock_1 (.out(CLK));
  Register #(.width(32)) u_PC (.D(multiplexer_2_out), .en(and_2_out), .clk(and_2_out), .Q(PC_q));  // open: clr
  Multiplexer #(.width(32)) multiplexer_2 (
    .in0(multiplexer_1_out), .in1(ALU), .out(multiplexer_2_out), .sel(ucprincipal_1_s_jalr));
  and and_2 (and_2_out, CLK, ~Stop);  // AND_Gate
  // Probe on PC
  // Probe on LD1
  // Probe on LD2
  // Probe on ALU
  Adder #(.width(32)) adder_2 (.a(32'h4), .b(PC_q), .out(adder_2_out));  // open: cin, cout
  memInstr meminstr_1 (.PC_address(PC_q), .Instruction(meminstr_1_instruction));
  // estagioIF_ID estagioif_id_1: pin names not known; wires that end beside it: adder_2_out, meminstr_1_instruction, PC_q, CLK, estagioif_id_1_p5, estagioif_id_1_p5, estagioif_id_1_p7, estagioif_id_1_p8, estagioif_id_1_p9
  decodificador decodificador_1 (
    .instrucao(estagioif_id_1_p9), .imm(decodificador_1_imm), .opcode(decodificador_1_opcode),
    .rd(decodificador_1_rd), .funct3(decodificador_1_funct3), .rs1(decodificador_1_rs1),
    .rs2(decodificador_1_rs2), .funct7(decodificador_1_funct7));
  ucPrincipal ucprincipal_1 (
    .BranchSrc(undriven), .opcode(decodificador_1_opcode), .MemRead(ucprincipal_1_memread),
    .MemWrite(ucprincipal_1_memwrite), .Jump(ucprincipal_1_jump), .Branch(ucprincipal_1_branch),
    .S_Jalr(ucprincipal_1_s_jalr), .RegWrite(ucprincipal_1_regwrite), .ALUOp(ucprincipal_1_aluop),
    .Auipc_uc(ucprincipal_1_auipc_uc), .ALUSrcB(ucprincipal_1_alusrcb), .Lui_uc(ucprincipal_1_lui_uc),
    .Stop(Stop), .MemToReg(ucprincipal_1_memtoreg), .PCSrc(ucprincipal_1_pcsrc));
  Multiplexer #(.width(32)) multiplexer_3 (.in0(WD), .in1(estagioif_id_1_p8), .out(multiplexer_3_out), .sel(Jump_WB));
  bancoRegistradores bancoregistradores_1 (
    .WD(multiplexer_3_out), .WR(rd_WB), .LD1(bancoregistradores_1_ld1), .LR1(decodificador_1_rs1),
    .LD2(bancoregistradores_1_ld2), .LR2(decodificador_1_rs2), .clk(CLK), .RegWrite(RegWrite_WB));
  // estagioID_EX estagioid_ex_1: pin names not known; wires that end beside it: estagioif_id_1_p7, estagioif_id_1_p8, ucprincipal_1_auipc_uc, ucprincipal_1_lui_uc, ucprincipal_1_pcsrc, ucprincipal_1_jump, ucprincipal_1_aluop, ucprincipal_1_regwrite, ucprincipal_1_alusrcb, ucprincipal_1_memtoreg, ucprincipal_1_memread, ucprincipal_1_memwrite, ucprincipal_1_branch, ucprincipal_1_s_jalr, bancoregistradores_1_ld1, bancoregistradores_1_ld2, decodificador_1_opcode, decodificador_1_rd, decodificador_1_funct3, decodificador_1_funct7, decodificador_1_imm, CLK, estagioid_ex_1_p23, estagioid_ex_1_p23, estagioid_ex_1_p25, estagioid_ex_1_p26, estagioid_ex_1_p27, estagioid_ex_1_p28, PCSrc_EX, estagioid_ex_1_p30, Jalr_EX, Branch_EX, estagioid_ex_1_p33, estagioid_ex_1_p34, estagioid_ex_1_p35, estagioid_ex_1_p36, estagioid_ex_1_p37, estagioid_ex_1_p38, estagioid_ex_1_p39, estagioid_ex_1_p40, estagioid_ex_1_p41, estagioid_ex_1_p42, estagioid_ex_1_p43, estagioid_ex_1_p44, estagioid_ex_1_p45, BranchSrc
  Multiplexer #(.width(32)) multiplexer_4 (
    .in0(estagioid_ex_1_p36), .in1(estagioid_ex_1_p37), .out(multiplexer_4_out), .sel(estagioid_ex_1_p35));
  Multiplexer #(.width(32)) multiplexer_5 (
    .in0(estagioid_ex_1_p38), .in1(estagioid_ex_1_p39), .out(LD2), .sel(estagioid_ex_1_p40));
  Multiplexer #(.width(32)) multiplexer_6 (
    .in0(multiplexer_4_out), .in1({32{1'b0}}), .out(multiplexer_6_out), .sel(estagioid_ex_1_p34));
  // ucULA ucula_1: pin names not known; wires that end beside it: estagioid_ex_1_p41, estagioid_ex_1_p42, estagioid_ex_1_p43, estagioid_ex_1_p44, ucula_1_p5
  ULA ula_1 (.B(LD2), .ALUControl(ucula_1_p5), .A(multiplexer_6_out), .sZero(ula_1_szero), .Result(ula_1_result));
  ucDesvio ucdesvio_1 (.Zero(ula_1_szero), .funct3(estagioid_ex_1_p42));  // open: BranchSrc
  estagioEX_MEM estagioex_mem_1 (
    .MemRead_EX(estagioid_ex_1_p27), .MemWrite_EX(estagioid_ex_1_p28), .CLK(CLK),
    .RegWrite_EX(estagioid_ex_1_p25), .MemToReg_EX(estagioid_ex_1_p26), .Jump_EX(estagioid_ex_1_p30),
    .ALUResult_EX(ula_1_result), .ld2_EX(estagioid_ex_1_p38), .rd_EX(estagioid_ex_1_p45),
    .PCplus4_EX(estagioid_ex_1_p33), .f3_EX(estagioid_ex_1_p42), .MemRead_MEM(estagioex_mem_1_memread_mem),
    .MemWrite_MEM(estagioex_mem_1_memwrite_mem), .RegWrite_MEM(estagioex_mem_1_regwrite_mem),
    .MemToReg_MEM(estagioex_mem_1_memtoreg_mem), .Jump_MEM(estagioex_mem_1_jump_mem), .ALUResult_MEM(ALU),
    .ld2_MEM(estagioex_mem_1_ld2_mem), .rd_MEM(estagioex_mem_1_rd_mem),
    .PCplus4_MEM(estagioex_mem_1_pcplus4_mem), .f3_MEM(estagioex_mem_1_f3_mem));
  ucEnderecamento ucenderecamento_1 (
    .Adress(ALU), .Funct3(estagioex_mem_1_f3_mem), .writeEnable(estagioex_mem_1_memwrite_mem),
    .byteEnable(ucenderecamento_1_byteenable), .Size(ucenderecamento_1_size), .Offset(offset),
    .signal_unsigned(sUnsigned));
  and and_3 (and_3_out, CLK, ~Stop);  // AND_Gate
  memDados memdados_1 (
    .Endereco(ALU), .clk(and_3_out), .MemRead(estagioex_mem_1_memread_mem),
    .byteEnable(ucenderecamento_1_byteenable), .dado(estagioex_mem_1_ld2_mem), .size(ucenderecamento_1_size),
    .offset(offset), .sUnsigned(sUnsigned), .Dados_lidos(memdados_1_dados_lidos));
  estagioMEM_WB estagiomem_wb_1 (
    .RegWrite_MEM(estagioex_mem_1_regwrite_mem), .MemToReg_MEM(estagioex_mem_1_memtoreg_mem),
    .Jump_MEM(estagioex_mem_1_jump_mem), .CLK(CLK), .MemData_MEM(memdados_1_dados_lidos),
    .ALUResult_MEM(ALU), .rd_MEM(estagioex_mem_1_rd_mem), .PCplus4_MEM(estagioex_mem_1_pcplus4_mem),
    .RegWrite_WB(estagiomem_wb_1_regwrite_wb), .MemToReg_WB(estagiomem_wb_1_memtoreg_wb),
    .Jump_WB(estagiomem_wb_1_jump_wb), .MemData_WB(estagiomem_wb_1_memdata_wb),
    .ALUResult_WB(estagiomem_wb_1_aluresult_wb), .rd_WB(estagiomem_wb_1_rd_wb),
    .PCplus4_WB(estagiomem_wb_1_pcplus4_wb));
  Multiplexer #(.width(32)) multiplexer_7 (
    .in0(estagiomem_wb_1_aluresult_wb), .in1(estagiomem_wb_1_memdata_wb), .out(WD),
    .sel(estagiomem_wb_1_memtoreg_wb));

  // Notes on the sheet:
  //   RegWrite
  //   MemToReg
  //   MemRead
  //   MemWrite
  //   PC + 4
  //   LUI
  //   AUIPC
  //   ID1_EX
  //   PC
  //   ID2_EX
  //   IMM
  //   ALUSrc_B
  //   f3
  //   f7
  //   AluOP
  //   rd
  //   Jump
  //   rs2
  //   f3
  //   memToReg
  //   Pc+4
  //   RD
  //   RegWrite
  //   Jump
  //   memRead
  //   ALU
  //   ID2
  //   MemWrite
  //   Pc+4
  //   RD
  //   RegWrite
  //   Jump
  //   ALU
  //   LD
  //   memToReg
endmodule
