// Logisim project simuladorFinal.circ as structural Verilog: 15 circuits, main circuit decodificador
module decodificador (
  input  [31:0] \instrução ,
  output [6:0] funct7,
  output [4:0] rs2,
  output [4:0] rs1,
  output [2:0] funct3,
  output [4:0] rd,
  output [6:0] opcode
);


  assign funct3 = \instrução [19:17];
  assign funct7 = \instrução [6:0];
  assign opcode = \instrução [31:25];
  assign rd = \instrução [24:20];
  assign rs1 = \instrução [16:12];
  assign rs2 = \instrução [11:7];
endmodule

module extensorSinal_16 (
  input  [15:0] entrada,
  output [31:0] \saída 
);

  // Probe on entrada
  // Probe on {{17{entrada[15]}}, entrada[14:0]}

  assign \saída  = {{17{entrada[15]}}, entrada[14:0]};
endmodule

module extensorSinal_12 (
  input  [11:0] entrada,
  output [31:0] \saída 
);

  // Probe on entrada
  // Probe on {{21{entrada[11]}}, entrada[10:0]}

  assign \saída  = {{21{entrada[11]}}, entrada[10:0]};
endmodule

module extensorSinal_13 (
  input  [12:0] entrada,
  output [31:0] \saída 
);

  // Probe on entrada
  // Probe on {{20{entrada[12]}}, entrada[11:0]}

  assign \saída  = {{20{entrada[12]}}, entrada[11:0]};
endmodule

module extensorSinal_20 (
  input  [19:0] entrada,
  output [31:0] \saída 
);

  // Probe on entrada
  // Probe on {{13{entrada[19]}}, entrada[18:0]}

  assign \saída  = {{13{entrada[19]}}, entrada[18:0]};
endmodule

module extensorSinal_21 (
  input  [20:0] entrada,
  output [31:0] \saída 
);

  // Probe on entrada
  // Probe on {{12{entrada[20]}}, entrada[19:0]}

  assign \saída  = {{12{entrada[20]}}, entrada[19:0]};
endmodule

module ucPrincipal (
  input  [6:0] opcode,
  input  Zero,
  input  Bne,
  output R_type,
  output I_type,
  output RegWrite,
  output ALUSrc,
  output PCSrc,
  output L_type,
  output S_type,
  output MemToReg,
  output MemRead,
  output MemWrite,
  output Branch,
  output J_type,
  output [1:0] ALUOp,
  output B_type
);

  wire multiplexer_1_out, not_1_out;

  and R (R_type, opcode[0], opcode[1], ~opcode[2], ~opcode[3], opcode[4], opcode[5], ~opcode[6]);  // AND_Gate
  and I (I_type, opcode[0], opcode[1], ~opcode[2], ~opcode[3], opcode[4], ~opcode[5], ~opcode[6]);  // AND_Gate
  and L (L_type, opcode[0], opcode[1], ~opcode[2], ~opcode[3], ~opcode[4], ~opcode[5], ~opcode[6]);  // AND_Gate
  and S (MemWrite, opcode[0], opcode[1], ~opcode[2], ~opcode[3], ~opcode[4], opcode[5], ~opcode[6]);  // AND_Gate
  and J (J_type, opcode[0], opcode[1], opcode[2], opcode[3], ~opcode[4], opcode[5], opcode[6]);  // AND_Gate
  and B (B_type, opcode[0], opcode[1], ~opcode[2], ~opcode[3], ~opcode[4], opcode[5], opcode[6]);  // AND_Gate
  or or_1 (RegWrite, J_type, L_type, I_type, R_type);
  or or_2 (ALUOp[1], R_type, I_type);
  or or_3 (ALUOp[0], B_type, I_type);
  or or_4 (ALUSrc, MemWrite, L_type, I_type);
  and and_1 (PCSrc, B_type, multiplexer_1_out);
  not not_1 (not_1_out, Zero);
  Multiplexer #(.enable("false")) multiplexer_1 (.in0(not_1_out), .in1(Zero), .out(multiplexer_1_out), .sel(Bne));

  assign Branch = B_type;
  assign MemRead = L_type;
  assign MemToReg = L_type;
  assign S_type = MemWrite;

  // Notes on the sheet:
  //   0110011
  //   0010011
  //   0000011
  //   0100011
  //   1101111
  //   1100011
  //   ___________________________________________
  //   ___________________________________________
  //   Instruções R
  //   ___________________________
  //   ___________________________
  //   Memória
  //   condicionais
  //   ____________
  //   ____________
  //   Desvios
  //   __________
  //   __________
  //   Desvios
  //   incondicionais
endmodule

module ucULA (
  input  [2:0] funct3,
  input  [6:0] funct7,
  output [3:0] ALU_control_lines
);

  wire R_type;
  wire [2:0] bit_0_out;
  wire [3:0] bit_extender_1_out;

  assign bit_extender_1_out = {{3{1'b1}}, R_type};  // Bit_Extender bit_extender_1
  and bit_2 (bit_0_out[2], ~funct3[0], ~funct3[1], ~funct3[2], funct7[5]);  // AND_Gate
  assign ALU_control_lines = bit_extender_1_out & {1'b0, bit_0_out};  // AND_Gate and_1, 4 bits wide
  and bit_1 (bit_0_out[1], ~funct3[0], ~funct3[1], ~funct3[2]);  // AND_Gate
  and bit_0 (bit_0_out[0], ~funct3[0], funct3[1], funct3[2]);  // AND_Gate
endmodule

module main (
);

  wire ALUSrc, B_type, Bne, Branch, CLK, I_type, J_type, JR, Jump, L_type, Link, MemRead, MemToReg, MemWrite,
       PCSrc, R_type, RegDst, RegWrite, S_type, ula_1_overflow, Zero;
  wire [1:0] ALUOp;
  wire [2:0] decodificador_1_funct3;
  wire [3:0] ucula_1_alu_control_lines;
  wire [4:0] decodificador_1_rd, decodificador_1_rs1, decodificador_1_rs2, multiplexer_4_out,
       multiplexer_5_out;
  wire [6:0] decodificador_1_funct7, decodificador_1_opcode;
  wire [25:0] undriven;
  wire [31:0] adder_1_out, adder_2_out, bancoregistradores_1_ld1, bancoregistradores_1_ld2,
       conc_1_jump_address, datamem_1_dados_lidos, immExt, immgen_1_imm, LD1, LD2, meminstr_1_instruction,
       multiplexer_1_out, multiplexer_2_out, multiplexer_3_out, multiplexer_6_out, PC___4, PC_q,
       register_1_q, shifter_1_out, ula_1_result, WD;

  Multiplexer #(.width(32), .enable("false")) multiplexer_1 (
    .in0(PC___4), .in1(adder_1_out), .out(multiplexer_1_out), .sel(PCSrc));
  Adder #(.width(32)) adder_1 (.a(PC___4), .b(immExt), .out(adder_1_out));  // open: cin, cout
  Register #(.width(32)) register_1 (.D(adder_2_out), .en(CLK), .Q(register_1_q), .clk(CLK));  // open: clr
  Multiplexer #(.width(32), .enable("false")) multiplexer_2 (
    .in0(multiplexer_1_out), .in1(conc_1_jump_address), .out(multiplexer_2_out), .sel(Jump));
  Adder #(.width(32)) adder_2 (.a(register_1_q), .b(32'h1), .out(adder_2_out));  // open: cin, cout
  // Probe on register_1_q
  Multiplexer #(.width(32), .enable("false")) multiplexer_3 (
    .in0(multiplexer_2_out), .in1(LD1), .out(multiplexer_3_out), .sel(JR));
  Register #(.width(32)) PC (.D(multiplexer_3_out), .Q(PC_q), .clk(CLK));  // open: en, clr
  Adder #(.width(32)) adder_3 (.a(32'h4), .b(PC_q), .out(PC___4));  // open: cin, cout
  conc conc_1 (.jump_address(conc_1_jump_address), .pc___4(PC___4), .address(undriven));
  MemInstr meminstr_1 (.PC_address(PC_q), .Instruction(meminstr_1_instruction));
  decodificador decodificador_1 (
    .\instrução (meminstr_1_instruction), .opcode(decodificador_1_opcode), .rd(decodificador_1_rd),
    .funct3(decodificador_1_funct3), .rs1(decodificador_1_rs1), .rs2(decodificador_1_rs2),
    .funct7(decodificador_1_funct7));
  immGen immgen_1 (
    .\instrução (meminstr_1_instruction), .imm(immgen_1_imm), .J_type(J_type), .S_type(S_type),
    .B_type(B_type));
  Multiplexer #(.width(5), .enable("false")) multiplexer_4 (
    .in0(decodificador_1_rs2), .in1(decodificador_1_rd), .out(multiplexer_4_out), .sel(RegDst));
  Multiplexer #(.width(5), .enable("false")) multiplexer_5 (
    .in0(multiplexer_4_out), .in1({5{1'b1}}), .out(multiplexer_5_out), .sel(Link));
  ucPrincipal ucprincipal_1 (
    .opcode(decodificador_1_opcode), .RegWrite(RegWrite), .ALUSrc(ALUSrc), .MemToReg(MemToReg),
    .MemRead(MemRead), .MemWrite(MemWrite), .PCSrc(PCSrc), .Branch(Branch), .ALUOp(ALUOp), .R_type(R_type),
    .I_type(I_type), .L_type(L_type), .S_type(S_type), .J_type(J_type), .B_type(B_type), .Bne(Bne),
    .Zero(Zero));
  Multiplexer #(.width(32), .enable("false")) multiplexer_6 (
    .in0(WD), .in1(PC___4), .out(multiplexer_6_out), .sel(Link));
  bancoRegistradores bancoregistradores_1 (
    .WD(multiplexer_6_out), .WR(multiplexer_5_out), .LD1(bancoregistradores_1_ld1),
    .LR1(decodificador_1_rs1), .LD2(bancoregistradores_1_ld2), .LR2(decodificador_1_rs2), .clk(CLK),
    .RegWrite(RegWrite));
  ucULA ucula_1 (
    .ALU_control_lines(ucula_1_alu_control_lines), .funct3(decodificador_1_funct3),
    .funct7(decodificador_1_funct7));
  Multiplexer #(.width(32), .enable("false")) multiplexer_7 (
    .in0(immgen_1_imm), .in1(shifter_1_out), .out(immExt), .sel(B_type));
  Shifter #(.width(32)) shifter_1 (.in(immgen_1_imm), .\dist (5'b00010), .out(shifter_1_out));
  Clock clock_1 (.out(CLK));
  // Probe on bancoregistradores_1_ld1
  Multiplexer #(.width(32), .enable("false")) multiplexer_8 (
    .in0(bancoregistradores_1_ld2), .in1(immgen_1_imm), .out(LD2), .sel(ALUSrc));
  ula ula_1 (
    .ZERO(Zero), .Result(ula_1_result), .Overflow(ula_1_overflow), .A(bancoregistradores_1_ld1), .B(LD2),
    .ALU_control_lines(ucula_1_alu_control_lines));
  LED led_1 (.in(ula_1_overflow));
  datamem datamem_1 (
    .adress(ula_1_result), .Escreve_dado(bancoregistradores_1_ld2), .MemWrite(MemWrite), .clk(CLK),
    .MemRead(MemRead), .Dados_lidos(datamem_1_dados_lidos));  // open: clear
  Multiplexer #(.width(32), .enable("false")) multiplexer_9 (
    .in0(ula_1_result), .in1(datamem_1_dados_lidos), .out(WD), .sel(MemToReg));

  // Notes on the sheet:
  //   jr e jump?
  //   addr
endmodule

module conc (
  input  [25:0] address,
  input  [31:0] pc___4,
  output [31:0] jump_address
);


  assign jump_address = {pc___4[31:28], {8{1'b0}}, address[17:0], 2'b00};

  // Other names for the same wires on the sheet: addr[25:0] = address
endmodule

module ula (
  input  [31:0] A,
  input  [31:0] B,
  input  [3:0] ALU_control_lines,
  output ZERO,
  output [31:0] Result,
  output Overflow
);

  wire comparator_1_lt;
  wire [31:0] adder_1_out, and_1_out, bit_extender_1_out, nor_1_out, or_1_out, subtractor_1_out, undriven,
       undriven_2, xor_1_out;

  Comparator #(.width(32)) comparator_1 (.a(A), .b(B), .lt(comparator_1_lt));  // open: gt, eq
  assign and_1_out = A & B;  // AND_Gate and_1, 32 bits wide
  assign or_1_out = A | B;  // OR_Gate or_1, 32 bits wide
  Adder #(.width(32)) adder_1 (.a(A), .b(B), .out(adder_1_out));  // open: cin, cout
  assign xor_1_out = A ^ B;  // XOR_Gate xor_1, 32 bits wide
  assign bit_extender_1_out = {{31{1'b0}}, comparator_1_lt};  // Bit_Extender bit_extender_1
  assign nor_1_out = ~(A | B);  // NOR_Gate nor_1, 32 bits wide
  Subtractor #(.width(32)) subtractor_1 (.a(A), .b(B), .out(subtractor_1_out));  // open: bin, bout
  // Probe on A
  // Probe on B
  zero zero_1 (.Result(Result), .ZERO(ZERO));
  Multiplexer #(.select(4), .width(32), .enable("false")) multiplexer_1 (
    .in0(and_1_out), .in1(or_1_out), .in2(adder_1_out), .in3(xor_1_out), .in4(bit_extender_1_out),
    .in5(nor_1_out), .in6(subtractor_1_out), .in7(undriven_2), .in8(undriven), .in9({32{1'b0}}),
    .in10({32{1'b0}}), .in11({32{1'b0}}), .in12({32{1'b0}}), .in13({32{1'b0}}), .in14({32{1'b0}}),
    .in15({32{1'b0}}), .out(Result), .sel(ALU_control_lines));
  // Probe on Result
  overflow overflow_1 (.out_5(Overflow), .Operador(ALU_control_lines), .a(A), .b(B), .Result(Result));
endmodule

module overflow (
  input  [31:0] a,
  input  [31:0] b,
  input  [31:0] Result,
  input  [3:0] Operador,
  output out_5
);

  wire and_1_out, and_2_out, and_3_out, and_4_out, and_5_out, and_6_out;

  and and_1 (and_1_out, Operador[0], ~Operador[1], Operador[2], ~Operador[3]);  // AND_Gate
  and and_2 (and_2_out, ~Operador[0], Operador[1], Operador[2], ~Operador[3]);  // AND_Gate
  and and_3 (and_3_out, Result[31], ~b[31], ~a[31], and_1_out);  // AND_Gate
  and and_4 (and_4_out, ~Result[31], b[31], a[31], and_1_out);  // AND_Gate
  and and_5 (and_5_out, Result[31], b[31], ~a[31], and_2_out);  // AND_Gate
  and and_6 (and_6_out, ~Result[31], ~b[31], a[31], and_2_out);  // AND_Gate
  or or_1 (out_5, and_3_out, and_4_out, and_5_out, and_6_out);
endmodule

module zero (
  input  [31:0] Result,
  output ZERO
);

  Comparator #(.width(32)) comparator_1 (.a({32{1'b0}}), .b(Result), .eq(ZERO));  // open: gt, lt
endmodule

module bancoRegistradores (
  input  [4:0] LR1,
  input  [31:0] WD,
  input  [4:0] WR,
  input  [4:0] LR2,
  input  clk,
  input  RegWrite,
  output [31:0] LD1,
  output [31:0] LD2
);

  wire demultiplexer_2_out0, demultiplexer_2_out1, demultiplexer_2_out2, demultiplexer_2_out3,
       demultiplexer_2_out4, demultiplexer_2_out5, demultiplexer_2_out6, demultiplexer_2_out7,
       demultiplexer_2_out8, demultiplexer_2_out9, demultiplexer_2_out10, demultiplexer_2_out11,
       demultiplexer_2_out12, demultiplexer_2_out13, demultiplexer_2_out14, demultiplexer_2_out15,
       demultiplexer_2_out16, demultiplexer_2_out17, demultiplexer_2_out18, demultiplexer_2_out19,
       demultiplexer_2_out20, demultiplexer_2_out21, demultiplexer_2_out22, demultiplexer_2_out23,
       demultiplexer_2_out24, demultiplexer_2_out25, demultiplexer_2_out26, demultiplexer_2_out27,
       demultiplexer_2_out28, demultiplexer_2_out29, demultiplexer_2_out30, demultiplexer_2_out31;
  wire [31:0] _00_q, _01_q, _02_q, _03_q, _04_q, _05_q, _06_q, _07_q, _08_q, _09_q, _10_q, _11_q, _12_q,
       _13_q, _14_q, _15_q, _16_q, _17_q, _18_q, _19_q, _20_q, _21_q, _22_q, _23_q, _24_q, _25_q, _26_q,
       _27_q, _28_q, _29_q, _30_q, _31_q, demultiplexer_1_out0, demultiplexer_1_out1, demultiplexer_1_out2,
       demultiplexer_1_out3, demultiplexer_1_out4, demultiplexer_1_out5, demultiplexer_1_out6,
       demultiplexer_1_out7, demultiplexer_1_out8, demultiplexer_1_out9, demultiplexer_1_out10,
       demultiplexer_1_out11, demultiplexer_1_out12, demultiplexer_1_out13, demultiplexer_1_out14,
       demultiplexer_1_out15, demultiplexer_1_out16, demultiplexer_1_out17, demultiplexer_1_out18,
       demultiplexer_1_out19, demultiplexer_1_out20, demultiplexer_1_out21, demultiplexer_1_out22,
       demultiplexer_1_out23, demultiplexer_1_out24, demultiplexer_1_out25, demultiplexer_1_out26,
       demultiplexer_1_out27, demultiplexer_1_out28, demultiplexer_1_out29, demultiplexer_1_out30,
       demultiplexer_1_out31;

  // Probe on WD
  Demultiplexer #(.select(5), .width(32), .enable("false")) demultiplexer_1 (
    .out0(demultiplexer_1_out0), .out1(demultiplexer_1_out1), .out2(demultiplexer_1_out2),
    .out3(demultiplexer_1_out3), .out4(demultiplexer_1_out4), .out5(demultiplexer_1_out5),
    .out6(demultiplexer_1_out6), .out7(demultiplexer_1_out7), .out8(demultiplexer_1_out8),
    .out9(demultiplexer_1_out9), .out10(demultiplexer_1_out10), .out11(demultiplexer_1_out11),
    .out12(demultiplexer_1_out12), .out13(demultiplexer_1_out13), .out14(demultiplexer_1_out14),
    .out15(demultiplexer_1_out15), .out16(demultiplexer_1_out16), .out17(demultiplexer_1_out17),
    .out18(demultiplexer_1_out18), .out19(demultiplexer_1_out19), .out20(demultiplexer_1_out20),
    .out21(demultiplexer_1_out21), .out22(demultiplexer_1_out22), .out23(demultiplexer_1_out23),
    .out24(demultiplexer_1_out24), .out25(demultiplexer_1_out25), .out26(demultiplexer_1_out26),
    .out27(demultiplexer_1_out27), .out28(demultiplexer_1_out28), .out29(demultiplexer_1_out29),
    .out30(demultiplexer_1_out30), .out31(demultiplexer_1_out31), .in(WD), .sel(WR));
  Register #(.width(32)) _00 (.D(demultiplexer_1_out0), .Q(_00_q), .clk(clk), .clr(demultiplexer_2_out0));  // open: en
  Register #(.width(32)) _01 (.D(demultiplexer_1_out1), .en(demultiplexer_2_out1), .Q(_01_q), .clk(clk));  // open: clr
  Register #(.width(32)) _02 (.D(demultiplexer_1_out2), .en(demultiplexer_2_out2), .Q(_02_q), .clk(clk));  // open: clr
  Register #(.width(32)) _03 (.D(demultiplexer_1_out3), .en(demultiplexer_2_out3), .Q(_03_q), .clk(clk));  // open: clr
  Register #(.width(32)) _04 (.D(demultiplexer_1_out4), .en(demultiplexer_2_out4), .Q(_04_q), .clk(clk));  // open: clr
  Register #(.width(32)) _05 (.D(demultiplexer_1_out5), .en(demultiplexer_2_out5), .Q(_05_q), .clk(clk));  // open: clr
  Register #(.width(32)) _06 (.D(demultiplexer_1_out6), .en(demultiplexer_2_out6), .Q(_06_q), .clk(clk));  // open: clr
  Register #(.width(32)) _07 (.D(demultiplexer_1_out7), .en(demultiplexer_2_out7), .Q(_07_q), .clk(clk));  // open: clr
  Register #(.width(32)) _08 (.D(demultiplexer_1_out8), .en(demultiplexer_2_out8), .Q(_08_q), .clk(clk));  // open: clr
  Register #(.width(32)) _09 (.D(demultiplexer_1_out9), .en(demultiplexer_2_out9), .Q(_09_q), .clk(clk));  // open: clr
  Register #(.width(32)) _10 (
    .D(demultiplexer_1_out10), .en(demultiplexer_2_out10), .Q(_10_q), .clk(clk));  // open: clr
  Register #(.width(32)) _11 (
    .D(demultiplexer_1_out11), .en(demultiplexer_2_out11), .Q(_11_q), .clk(clk));  // open: clr
  Register #(.width(32)) _12 (
    .D(demultiplexer_1_out12), .en(demultiplexer_2_out12), .Q(_12_q), .clk(clk));  // open: clr
  Register #(.width(32)) _13 (
    .D(demultiplexer_1_out13), .en(demultiplexer_2_out13), .Q(_13_q), .clk(clk));  // open: clr
  Register #(.width(32)) _14 (
    .D(demultiplexer_1_out14), .en(demultiplexer_2_out14), .Q(_14_q), .clk(clk));  // open: clr
  Register #(.width(32)) _15 (
    .D(demultiplexer_1_out15), .en(demultiplexer_2_out15), .Q(_15_q), .clk(clk));  // open: clr
  Register #(.width(32)) _16 (
    .D(demultiplexer_1_out16), .en(demultiplexer_2_out16), .Q(_16_q), .clk(clk));  // open: clr
  Register #(.width(32)) _17 (
    .D(demultiplexer_1_out17), .en(demultiplexer_2_out17), .Q(_17_q), .clk(clk));  // open: clr
  Register #(.width(32)) _18 (
    .D(demultiplexer_1_out18), .en(demultiplexer_2_out18), .Q(_18_q), .clk(clk));  // open: clr
  Register #(.width(32)) _19 (
    .D(demultiplexer_1_out19), .en(demultiplexer_2_out19), .Q(_19_q), .clk(clk));  // open: clr
  Register #(.width(32)) _20 (
    .D(demultiplexer_1_out20), .en(demultiplexer_2_out20), .Q(_20_q), .clk(clk));  // open: clr
  Register #(.width(32)) _21 (
    .D(demultiplexer_1_out21), .en(demultiplexer_2_out21), .Q(_21_q), .clk(clk));  // open: clr
  Register #(.width(32)) _22 (
    .D(demultiplexer_1_out22), .en(demultiplexer_2_out22), .Q(_22_q), .clk(clk));  // open: clr
  Register #(.width(32)) _23 (
    .D(demultiplexer_1_out23), .en(demultiplexer_2_out23), .Q(_23_q), .clk(clk));  // open: clr
  Register #(.width(32)) _24 (
    .D(demultiplexer_1_out24), .en(demultiplexer_2_out24), .Q(_24_q), .clk(clk));  // open: clr
  Register #(.width(32)) _25 (
    .D(demultiplexer_1_out25), .en(demultiplexer_2_out25), .Q(_25_q), .clk(clk));  // open: clr
  Register #(.width(32)) _26 (
    .D(demultiplexer_1_out26), .en(demultiplexer_2_out26), .Q(_26_q), .clk(clk));  // open: clr
  Register #(.width(32)) _27 (
    .D(demultiplexer_1_out27), .en(demultiplexer_2_out27), .Q(_27_q), .clk(clk));  // open: clr
  Register #(.width(32)) _28 (
    .D(demultiplexer_1_out28), .en(demultiplexer_2_out28), .Q(_28_q), .clk(clk));  // open: clr
  Register #(.width(32)) _29 (
    .D(demultiplexer_1_out29), .en(demultiplexer_2_out29), .Q(_29_q), .clk(clk));  // open: clr
  Register #(.width(32)) _30 (
    .D(demultiplexer_1_out30), .en(demultiplexer_2_out30), .Q(_30_q), .clk(clk));  // open: clr
  Register #(.width(32)) _31 (
    .D(demultiplexer_1_out31), .en(demultiplexer_2_out31), .Q(_31_q), .clk(clk));  // open: clr
  Demultiplexer #(.select(5), .enable("false")) demultiplexer_2 (
    .out0(demultiplexer_2_out0), .out1(demultiplexer_2_out1), .out2(demultiplexer_2_out2),
    .out3(demultiplexer_2_out3), .out4(demultiplexer_2_out4), .out5(demultiplexer_2_out5),
    .out6(demultiplexer_2_out6), .out7(demultiplexer_2_out7), .out8(demultiplexer_2_out8),
    .out9(demultiplexer_2_out9), .out10(demultiplexer_2_out10), .out11(demultiplexer_2_out11),
    .out12(demultiplexer_2_out12), .out13(demultiplexer_2_out13), .out14(demultiplexer_2_out14),
    .out15(demultiplexer_2_out15), .out16(demultiplexer_2_out16), .out17(demultiplexer_2_out17),
    .out18(demultiplexer_2_out18), .out19(demultiplexer_2_out19), .out20(demultiplexer_2_out20),
    .out21(demultiplexer_2_out21), .out22(demultiplexer_2_out22), .out23(demultiplexer_2_out23),
    .out24(demultiplexer_2_out24), .out25(demultiplexer_2_out25), .out26(demultiplexer_2_out26),
    .out27(demultiplexer_2_out27), .out28(demultiplexer_2_out28), .out29(demultiplexer_2_out29),
    .out30(demultiplexer_2_out30), .out31(demultiplexer_2_out31), .in(RegWrite), .sel(WR));
  Multiplexer #(.select(5), .width(32), .enable("false")) multiplexer_1 (
    .in0(_00_q), .in1(_01_q), .in2(_02_q), .in3(_03_q), .in4(_04_q), .in5(_05_q), .in6(_06_q), .in7(_07_q),
    .in8(_08_q), .in9(_09_q), .in10(_10_q), .in11(_11_q), .in12(_12_q), .in13(_13_q), .in14(_14_q),
    .in15(_15_q), .in16(_16_q), .in17(_17_q), .in18(_18_q), .in19(_19_q), .in20(_20_q), .in21(_21_q),
    .in22(_22_q), .in23(_23_q), .in24(_24_q), .in25(_25_q), .in26(_26_q), .in27(_27_q), .in28(_28_q),
    .in29(_29_q), .in30(_30_q), .in31(_31_q), .out(LD1), .sel(LR1));
  Multiplexer #(.select(5), .width(32), .enable("false")) multiplexer_2 (
    .in0(_00_q), .in1(_01_q), .in2(_02_q), .in3(_03_q), .in4(_04_q), .in5(_05_q), .in6(_06_q), .in7(_07_q),
    .in8(_08_q), .in9(_09_q), .in10(_10_q), .in11(_11_q), .in12(_12_q), .in13(_13_q), .in14(_14_q),
    .in15(_15_q), .in16(_16_q), .in17(_17_q), .in18(_18_q), .in19(_19_q), .in20(_20_q), .in21(_21_q),
    .in22(_22_q), .in23(_23_q), .in24(_24_q), .in25(_25_q), .in26(_26_q), .in27(_27_q), .in28(_28_q),
    .in29(_29_q), .in30(_30_q), .in31(_31_q), .out(LD2), .sel(LR2));
endmodule

module immGen (
  input  [31:0] \instrução ,
  input  B_type,
  input  S_type,
  input  J_type,
  output [31:0] imm
);

  wire [1:0] or_2_out;
  wire [31:0] \extensorsinal_12_1_saída , \extensorsinal_12_2_saída , \extensorsinal_13_1_saída ,
       \extensorsinal_21_1_saída ;

  extensorSinal_12 extensorsinal_12_1 (.entrada(\instrução [31:20]), .\saída (\extensorsinal_12_1_saída ));
  extensorSinal_12 extensorsinal_12_2 (
    .entrada({\instrução [31:25], \instrução [11:7]}), .\saída (\extensorsinal_12_2_saída ));
  extensorSinal_13 extensorsinal_13_1 (
    .entrada({\instrução [31], \instrução [7], \instrução [30:25], \instrução [11:8], 1'b0}),
    .\saída (\extensorsinal_13_1_saída ));
  extensorSinal_21 extensorsinal_21_1 (
    .entrada({\instrução [31], \instrução [19:12], \instrução [20], \instrução [30:21], 1'b0}),
    .\saída (\extensorsinal_21_1_saída ));
  extensorSinal_20 extensorsinal_20_1 (.entrada(\instrução [31:12]));  // open: saída
  or or_1 (or_2_out[1], B_type, J_type);
  // Probe on imm
  Multiplexer #(.select(2), .width(32), .enable("false")) multiplexer_1 (
    .in0(\extensorsinal_12_1_saída ), .in1(\extensorsinal_12_2_saída ), .in2(\extensorsinal_13_1_saída ),
    .in3(\extensorsinal_21_1_saída ), .out(imm), .sel(or_2_out));
  or or_2 (or_2_out[0], J_type, S_type);

  // Other names for the same wires on the sheet: B_type_imm[12:1] = {\instrução [31], \instrução [7], \instrução [30:25], \instrução [11:8]};
  //   imm_5[4:0] = \instrução [11:7]; S_type_imm[11:0] = {\instrução [31:25], \instrução [11:7]};
  //   I_type_imm[11:0] = \instrução [31:20]; imm_12[11:0] = \instrução [31:20]; imm_20[19:0] = \instrução [31:12];
  //   J_type_imm[20:1] = {\instrução [31], \instrução [19:12], \instrução [20], \instrução [30:21]};
  //   U_type_imm[19:0] = \instrução [31:12]; imm_7[6:0] = \instrução [31:25]

  // Notes on the sheet:
  //   Tipo I
  //   Tipo S
  //   Tipo B
  //   Tipo U
  //   Tipo J
endmodule
