// Logisim project ucPrincipal.circ as structural Verilog: 1 circuit, main circuit ucPrincipal
module ucPrincipal (
  input  [6:0] opcode,
  input  Zero,
  input  Bne,
  output RegWrite,
  output ALUSrc,
  output PCSrc,
  output [1:0] ImmSrc,
  output [1:0] ALUOp,
  output MemToReg,
  output MemRead,
  output MemWrite,
  output Branch,
  output Jalr,
  output Jump,
  output Stop
);

  wire and_1_out, Auipc, E, I_type, Jal, Lui, multiplexer_1_out, not_1_out, R_type;

  and R (R_type, opcode[0], opcode[1], ~opcode[2], ~opcode[3], opcode[4], opcode[5], ~opcode[6]);  // AND_Gate
  and I (I_type, opcode[0], opcode[1], ~opcode[2], ~opcode[3], opcode[4], ~opcode[5], ~opcode[6]);  // AND_Gate
  and Load (MemRead, opcode[0], opcode[1], ~opcode[2], ~opcode[3], ~opcode[4], ~opcode[5], ~opcode[6]);  // AND_Gate
  and S (MemWrite, opcode[0], opcode[1], ~opcode[2], ~opcode[3], ~opcode[4], opcode[5], ~opcode[6]);  // AND_Gate
  and B (ALUOp[0], opcode[0], opcode[1], ~opcode[2], ~opcode[3], ~opcode[4], opcode[5], opcode[6]);  // AND_Gate
  and u_Jal (Jal, opcode[0], opcode[1], opcode[2], opcode[3], ~opcode[4], opcode[5], opcode[6]);  // AND_Gate
  and u_Jalr (Jalr, opcode[0], opcode[1], opcode[2], ~opcode[3], ~opcode[4], opcode[5], opcode[6]);  // AND_Gate
  and u_Lui (Lui, opcode[0], opcode[1], opcode[2], ~opcode[3], opcode[4], opcode[5], ~opcode[6]);  // AND_Gate
  and u_Auipc (Auipc, opcode[0], opcode[1], opcode[2], ~opcode[3], opcode[4], ~opcode[5], ~opcode[6]);  // AND_Gate
  and u_E (E, opcode[0], opcode[1], ~opcode[2], ~opcode[3], opcode[4], opcode[5], opcode[6]);  // AND_Gate
  or or_1 (RegWrite, Jal, Jalr, MemRead, I_type, R_type);
  or or_2 (ALUOp[1], R_type, I_type);
  or or_3 (ALUSrc, MemWrite, Jalr, MemRead, I_type);
  nor nor_1 (Stop, R_type, I_type, MemRead, MemWrite, ALUOp[0], Jal, Jalr, Lui, Auipc, E);
  and and_1 (and_1_out, ALUOp[0], multiplexer_1_out);
  or or_4 (PCSrc, Jal, and_1_out);
  not not_1 (not_1_out, Zero);
  Multiplexer #(.enable("false")) multiplexer_1 (.in0(Zero), .in1(not_1_out), .out(multiplexer_1_out), .sel(Bne));
  or or_5 (ImmSrc[1], Jal, ALUOp[0]);
  or or_6 (ImmSrc[0], MemWrite, Jal);
  or or_7 (Jump, Jal, Jalr);

  assign Branch = ALUOp[0];
  assign MemToReg = MemRead;

  // Other names for the same wires on the sheet: B_type = ALUOp[0]; Load = MemRead; S_type = MemWrite

  // Notes on the sheet:
  //   0110011
  //   0010011
  //   0000011
  //   0100011
  //   1100011
  //   1101111
  //   1100111
  //   0110111
  //   1100111
  //   1110011
endmodule
